// Logisim project 16BitRegister.circ as structural Verilog: 1 circuit, main circuit main
module main (
  input  [15:0] Data,
  input  Store,
  input  Clock,
  input  Clear,
  input  Enable_Output,
  input  Output_Select,
  output [15:0] out_7,
  output [15:0] out_8
);

  wire [15:0] register_1_q;

  Register #(.width(16)) register_1 (.D(Data), .en(Store), .Q(register_1_q), .clk(Clock), .clr(Clear));
  Demultiplexer #(.width(16)) demultiplexer_1 (
    .out0(out_7), .out1(out_8), .in(register_1_q), .sel(Output_Select), .en(Enable_Output));
endmodule
