// Logisim project ALU.circ as structural Verilog: 1 circuit, main circuit main
module main (
  input  [15:0] A_Input,
  input  [15:0] B_Input,
  input  [2:0] Op_Select,
  output [15:0] Output,
  output [3:0] out_5
);

  wire adder_1_cout, and_1_out, and_2_out, and_3_out, and_5_out, and_6_out, and_7_out, and_8_out, and_9_out,
       and_10_out, and_11_out, bitselector_1_out, bitselector_2_out, not_1_out, not_2_out, not_3_out,
       not_4_out, not_5_out, not_6_out, not_7_out, not_8_out, not_9_out, or_4_out, or_5_out, or_6_out,
       pull_resistor_1_node, pull_resistor_2_node, subtractor_1_bout;
  wire [3:0] bit_extender_1_out;
  wire [15:0] adder_1_out, and_4_out, demultiplexer_1_out0, demultiplexer_1_out1, demultiplexer_1_out2,
       demultiplexer_1_out3, demultiplexer_1_out4, demultiplexer_1_out5, demultiplexer_1_out6,
       demultiplexer_2_out0, demultiplexer_2_out1, demultiplexer_2_out2, demultiplexer_2_out3,
       demultiplexer_2_out4, demultiplexer_2_out5, demultiplexer_2_out6, or_1_out, or_2_out, shifter_1_out,
       shifter_2_out, subtractor_1_out, xor_1_out;

  BitSelector #(.width(16)) bitselector_1 (.in(A_Input), .out(bitselector_1_out), .sel(4'b1111));
  BitSelector #(.width(16)) bitselector_2 (.in(B_Input), .out(bitselector_2_out), .sel(4'b1111));
  Demultiplexer #(.select(3), .width(16), .enable("false")) demultiplexer_1 (
    .out0(demultiplexer_1_out0), .out1(demultiplexer_1_out1), .out2(demultiplexer_1_out2),
    .out3(demultiplexer_1_out3), .out4(demultiplexer_1_out4), .out5(demultiplexer_1_out5),
    .out6(demultiplexer_1_out6), .in(A_Input), .sel(Op_Select));  // open: out7
  Demultiplexer #(.select(3), .width(16), .enable("false")) demultiplexer_2 (
    .out0(demultiplexer_2_out0), .out1(demultiplexer_2_out1), .out2(demultiplexer_2_out2),
    .out3(demultiplexer_2_out3), .out4(demultiplexer_2_out4), .out5(demultiplexer_2_out5),
    .out6(demultiplexer_2_out6), .in(B_Input), .sel(Op_Select));  // open: out7
  not not_1 (not_1_out, Op_Select[1]);
  assign or_1_out = demultiplexer_2_out5 | demultiplexer_2_out6;  // OR_Gate or_1, 16 bits wide
  not not_2 (not_2_out, Op_Select[0]);
  and and_1 (and_1_out, Op_Select[2], not_1_out, not_2_out);
  Bit_Extender #(.in_width(16), .out_width(4)) bit_extender_1 (.in(or_1_out), .out(bit_extender_1_out));
  Pull_Resistor pull_resistor_1 (.node(pull_resistor_1_node));
  Pull_Resistor pull_resistor_2 (.node(pull_resistor_2_node));
  and and_2 (and_2_out, Op_Select[0], Op_Select[1], not_3_out);
  not not_3 (not_3_out, Op_Select[2]);
  not not_4 (not_4_out, Op_Select[0]);
  not not_5 (not_5_out, Op_Select[1]);
  and and_3 (and_3_out, not_4_out, not_5_out, Op_Select[2]);
  assign xor_1_out = demultiplexer_1_out0 ^ demultiplexer_2_out0;  // XOR_Gate xor_1, 16 bits wide
  assign or_2_out = demultiplexer_1_out1 | demultiplexer_2_out1;  // OR_Gate or_2, 16 bits wide
  assign and_4_out = demultiplexer_1_out2 & demultiplexer_2_out2;  // AND_Gate and_4, 16 bits wide
  Adder #(.width(16)) adder_1 (
    .a(demultiplexer_1_out3), .b(demultiplexer_2_out3), .out(adder_1_out), .cin(pull_resistor_1_node),
    .cout(adder_1_cout));
  Subtractor #(.width(16)) subtractor_1 (
    .a(demultiplexer_1_out4), .b(demultiplexer_2_out4), .out(subtractor_1_out), .bin(pull_resistor_2_node),
    .bout(subtractor_1_bout));
  not not_6 (not_6_out, subtractor_1_bout);
  Shifter #(.width(16)) shifter_1 (.in(demultiplexer_1_out5), .\dist (bit_extender_1_out), .out(shifter_1_out));
  Shifter #(.width(16), .shift("lr")) shifter_2 (
    .in(demultiplexer_1_out6), .\dist (bit_extender_1_out), .out(shifter_2_out));
  or or_3 (out_5[0], adder_1_cout, and_5_out);
  and and_5 (and_5_out, not_6_out, and_1_out);
  and and_6 (and_6_out, not_7_out, bitselector_2_out, out_5[2]);
  not not_7 (not_7_out, bitselector_1_out);
  not not_8 (not_8_out, bitselector_2_out);
  Multiplexer #(.select(3), .width(16), .enable("false")) multiplexer_1 (
    .in0(xor_1_out), .in1(or_2_out), .in2(and_4_out), .in3(adder_1_out), .in4(subtractor_1_out),
    .in5(shifter_1_out), .in6(shifter_2_out), .out({out_5[2], Output[14:0]}), .sel(Op_Select));  // open: in7
  or or_4 (or_4_out, and_6_out, and_7_out);
  and and_7 (and_7_out, bitselector_1_out, not_8_out, not_9_out);
  and and_8 (and_8_out, not_7_out, not_8_out, out_5[2]);
  and and_9 (and_9_out, bitselector_1_out, bitselector_2_out, not_9_out);
  not not_9 (not_9_out, out_5[2]);
  Pull_Resistor pull_resistor_3 (.node({out_5[2], Output[14:0]}));
  and and_10 (and_10_out, or_4_out, and_3_out);
  or or_5 (or_5_out, and_8_out, and_9_out);
  and and_11 (and_11_out, or_5_out, and_2_out);
  or or_6 (or_6_out, out_5[2], Output[14], Output[13], Output[12], Output[11], Output[10], Output[9], Output[8], Output[7], Output[6], Output[5], Output[4], Output[3], Output[2], Output[1], Output[0]);
  not not_10 (out_5[1], or_6_out);
  or or_7 (out_5[3], and_10_out, and_11_out);

  assign Output[15] = out_5[2];
endmodule
