// Logisim project CPU.circ as structural Verilog: 1 circuit, main circuit main
module main (
  input  Reset,
  input  Clock,
  input  [15:0] Data_In,
  output [15:0] Data_Out,
  output [23:0] Address_Bus,
  output Read,
  output Write
);

  wire and_1_out, and_2_out, and_3_out, and_4_out, multiplexer_4_out, nor_1_out, not_1_out, not_2_out,
       not_3_out, not_4_out, not_5_out, not_6_out, not_7_out, not_8_out, not_9_out, not_10_out, or_1_out,
       or_2_out, or_12_out, or_13_out, or_16_out, pull_resistor_1_node, pull_resistor_4_node,
       pull_resistor_5_node, pull_resistor_12_node, pull_resistor_13_node, pull_resistor_22_node;
  wire [2:0] bit_extender_1_out, bit_extender_2_out, demultiplexer_1_out0, demultiplexer_1_out1,
       demultiplexer_1_out2, demultiplexer_1_out3, demultiplexer_1_out4, demultiplexer_1_out5,
       demultiplexer_1_out6, demultiplexer_1_out7, demultiplexer_2_out0, demultiplexer_2_out1,
       demultiplexer_2_out2, demultiplexer_2_out3, demultiplexer_2_out4, demultiplexer_2_out5,
       demultiplexer_2_out6, demultiplexer_2_out7, multiplexer_1_out, multiplexer_2_out, or_4_out, or_5_out,
       or_6_out, or_7_out, or_8_out, or_9_out, or_10_out, or_11_out, rom_1_data_2, rom_1_data_3,
       rom_1_data_4, rom_1_data_5, rom_1_data_6;
  wire [3:0] adder_1_out, ALU_out_5, Flags_q, Instruction_Step_Register_q;
  wire [5:0] bit_extender_5_out;
  wire [7:0] bit_extender_3_out;
  wire [9:0] bit_extender_6_out, bit_extender_7_out, or_14_out, shifter_3_out;
  wire [15:0] A_out_7, A_out_8, adder_2_out, B_out_7, B_out_8, Base_Pointer_out_7, Base_Pointer_out_8,
       bit_extender_4_out, C_out_7, C_out_8, controlled_buffer_1_out, controlled_buffer_2_out,
       controlled_buffer_3_out, controlled_buffer_4_out, D_out_7, D_out_8, Data_Bank_Register_out_7,
       Data_Bank_Register_out_8, demultiplexer_3_out0, demultiplexer_3_out1, Instruction_Register_q,
       multiplexer_3_out, or_3_out, or_15_out, or_17_out, or_18_out, Program_Bank_Register_out_7,
       Program_Bank_Register_out_8, Program_Counter_out_7, shifter_1_out, shifter_2_out, Stack_Pointer_out_7,
       Stack_Pointer_out_8;
  wire [23:0] bit_extender_8_out, bit_extender_9_out, or_19_out, shifter_4_out;
  wire [28:2] rom_1_data;

  Shifter #(.width(16), .shift("lr")) shifter_1 (.in(Instruction_Register_q), .\dist (4'b1001), .out(shifter_1_out));
  and and_1 (and_1_out, rom_1_data[2], not_2_out);
  and and_2 (and_2_out, rom_1_data[2], not_3_out);
  Demultiplexer #(.select(3), .width(3), .enable("false")) demultiplexer_1 (
    .out0(demultiplexer_1_out0), .out1(demultiplexer_1_out1), .out2(demultiplexer_1_out2),
    .out3(demultiplexer_1_out3), .out4(demultiplexer_1_out4), .out5(demultiplexer_1_out5),
    .out6(demultiplexer_1_out6), .out7(demultiplexer_1_out7), .in(rom_1_data[27:25]), .sel(multiplexer_1_out));
  Bit_Extender #(.in_width(16), .out_width(3)) bit_extender_1 (.in(shifter_1_out), .out(bit_extender_1_out));
  Bit_Extender #(.in_width(16), .out_width(3)) bit_extender_2 (.in(shifter_2_out), .out(bit_extender_2_out));
  Shifter #(.width(16), .shift("lr")) shifter_2 (.in(Instruction_Register_q), .\dist (4'b0110), .out(shifter_2_out));
  Demultiplexer #(.select(3), .width(3), .enable("false")) demultiplexer_2 (
    .out0(demultiplexer_2_out0), .out1(demultiplexer_2_out1), .out2(demultiplexer_2_out2),
    .out3(demultiplexer_2_out3), .out4(demultiplexer_2_out4), .out5(demultiplexer_2_out5),
    .out6(demultiplexer_2_out6), .out7(demultiplexer_2_out7), .in(rom_1_data_5), .sel(multiplexer_2_out));
  Multiplexer #(.width(3), .enable("false")) multiplexer_1 (
    .in0(rom_1_data_6), .in1(bit_extender_2_out), .out(multiplexer_1_out), .sel(and_2_out));
  Bit_Extender #(.in_width(16), .out_width(8)) bit_extender_3 (.in(or_3_out), .out(bit_extender_3_out));
  Register #(.width(16)) Instruction_Register (
    .D(or_3_out), .en(rom_1_data[15]), .Q(Instruction_Register_q), .clk(Clock), .clr(Reset));
  not not_1 (not_1_out, and_1_out);
  not not_2 (not_2_out, or_2_out);
  not not_3 (not_3_out, or_1_out);
  or or_1 (or_1_out, rom_1_data_6[0], rom_1_data_6[1], rom_1_data_6[2]);
  or or_2 (or_2_out, rom_1_data_4[0], rom_1_data_4[1], rom_1_data_4[2]);
  Pull_Resistor #(.pull(1)) pull_resistor_1 (.node(pull_resistor_1_node));
  assign or_3_out = demultiplexer_3_out0 | Data_Out;  // OR_Gate or_3, 16 bits wide
  assign or_4_out = demultiplexer_2_out0 | demultiplexer_1_out0;  // OR_Gate or_4, 3 bits wide
  assign or_5_out = demultiplexer_2_out1 | demultiplexer_1_out1;  // OR_Gate or_5, 3 bits wide
  assign or_6_out = demultiplexer_2_out2 | demultiplexer_1_out2;  // OR_Gate or_6, 3 bits wide
  assign or_7_out = demultiplexer_2_out3 | demultiplexer_1_out3;  // OR_Gate or_7, 3 bits wide
  Multiplexer #(.width(3), .enable("false")) multiplexer_2 (
    .in0(bit_extender_1_out), .in1(rom_1_data_4), .out(multiplexer_2_out), .sel(not_1_out));
  assign bit_extender_4_out = {{8{1'b0}}, bit_extender_3_out};  // Bit_Extender bit_extender_4
  assign controlled_buffer_1_out = or_12_out ? Instruction_Register_q : 16'bz;  // Controlled_Buffer controlled_buffer_1
  Pull_Resistor pull_resistor_2 (.node(controlled_buffer_1_out));
  Bit_Extender #(.in_width(16), .out_width(6)) bit_extender_5 (.in(controlled_buffer_1_out), .out(bit_extender_5_out));
  ROM #(.addrWidth(10), .dataWidth(29)) rom_1 (
    .addr(or_14_out),
    .data({rom_1_data[28:25], rom_1_data_6, rom_1_data_5, rom_1_data_4, rom_1_data[15:12], rom_1_data_3, rom_1_data[8:7], rom_1_data_2, rom_1_data[3:2], Read, Write}),
    .sel(pull_resistor_1_node));
  assign or_8_out = demultiplexer_2_out4 | demultiplexer_1_out4;  // OR_Gate or_8, 3 bits wide
  assign or_9_out = demultiplexer_2_out5 | demultiplexer_1_out5;  // OR_Gate or_9, 3 bits wide
  assign or_10_out = demultiplexer_2_out6 | demultiplexer_1_out6;  // OR_Gate or_10, 3 bits wide
  assign or_11_out = demultiplexer_2_out7 | demultiplexer_1_out7;  // OR_Gate or_11, 3 bits wide
  assign bit_extender_6_out = {{4{1'b0}}, bit_extender_5_out};  // Bit_Extender bit_extender_6
  Pull_Resistor pull_resistor_3 (.node({rom_1_data[28:25], rom_1_data_6, rom_1_data_5, rom_1_data_4, rom_1_data[15:12], rom_1_data_3, rom_1_data[8:7], rom_1_data_2, rom_1_data[3:2], Read, Write}));
  _16BitRegister_main A (
    .Data(or_3_out), .Store(or_4_out[2]), .Clock(Clock), .Clear(Reset), .Enable_Output(or_4_out[1]),
    .Output_Select(or_4_out[0]), .out_7(A_out_7), .out_8(A_out_8));
  _16BitRegister_main B (
    .Data(or_3_out), .Store(or_5_out[2]), .Clock(Clock), .Clear(Reset), .Enable_Output(or_5_out[1]),
    .Output_Select(or_5_out[0]), .out_7(B_out_7), .out_8(B_out_8));
  _16BitRegister_main C (
    .Data(or_3_out), .Store(or_6_out[2]), .Clock(Clock), .Clear(Reset), .Enable_Output(or_6_out[1]),
    .Output_Select(or_6_out[0]), .out_7(C_out_7), .out_8(C_out_8));
  _16BitRegister_main D (
    .Data(or_3_out), .Store(or_7_out[2]), .Clock(Clock), .Clear(Reset), .Enable_Output(or_7_out[1]),
    .Output_Select(or_7_out[0]), .out_7(D_out_7), .out_8(D_out_8));
  _16BitRegister_main Stack_Pointer (
    .Data(or_3_out), .Store(or_8_out[2]), .Clock(Clock), .Clear(Reset), .Enable_Output(or_8_out[1]),
    .Output_Select(or_8_out[0]), .out_7(Stack_Pointer_out_7), .out_8(Stack_Pointer_out_8));
  _16BitRegister_main Base_Pointer (
    .Data(or_3_out), .Store(or_9_out[2]), .Clock(Clock), .Clear(Reset), .Enable_Output(or_9_out[1]),
    .Output_Select(or_9_out[0]), .out_7(Base_Pointer_out_7), .out_8(Base_Pointer_out_8));
  _16BitRegister_main Program_Bank_Register (
    .Data(bit_extender_4_out), .Store(or_10_out[2]), .Clock(Clock), .Clear(Reset),
    .Enable_Output(or_10_out[1]), .Output_Select(or_10_out[0]), .out_7(Program_Bank_Register_out_7),
    .out_8(Program_Bank_Register_out_8));
  _16BitRegister_main Data_Bank_Register (
    .Data(bit_extender_4_out), .Store(or_11_out[2]), .Clock(Clock), .Clear(Reset),
    .Enable_Output(or_11_out[1]), .Output_Select(or_11_out[0]), .out_7(Data_Bank_Register_out_7),
    .out_8(Data_Bank_Register_out_8));
  or or_12 (or_12_out, Instruction_Step_Register_q[3], Instruction_Step_Register_q[2], Instruction_Step_Register_q[1]);
  Register #(.width(4)) Instruction_Step_Register (
    .D(adder_1_out), .en(pull_resistor_4_node), .Q(Instruction_Step_Register_q), .clk(not_4_out),
    .clr(or_13_out));
  Pull_Resistor #(.pull(1)) pull_resistor_4 (.node(pull_resistor_4_node));
  or or_13 (or_13_out, rom_1_data[3], Reset);
  not not_4 (not_4_out, Clock);
  Shifter #(.width(10)) shifter_3 (.in(bit_extender_6_out), .\dist (4'b0100), .out(shifter_3_out));
  Demultiplexer #(.width(16), .enable("false")) demultiplexer_3 (
    .out0(demultiplexer_3_out0), .out1(demultiplexer_3_out1), .in(Data_In), .sel(rom_1_data[28]));
  Pull_Resistor pull_resistor_5 (.node(pull_resistor_5_node));
  assign bit_extender_7_out = {{6{1'b0}}, Instruction_Step_Register_q};  // Bit_Extender bit_extender_7
  Pull_Resistor pull_resistor_6 (.node(Data_In));
  Pull_Resistor pull_resistor_7 (.node(Program_Bank_Register_out_8));
  Pull_Resistor pull_resistor_8 (.node(Data_Bank_Register_out_8));
  Multiplexer #(.width(16), .enable("false")) multiplexer_3 (
    .in0(or_3_out), .in1(adder_2_out), .out(multiplexer_3_out), .sel(multiplexer_4_out));
  Adder #(.width(4)) adder_1 (
    .a(Instruction_Step_Register_q), .b(4'b0001), .out(adder_1_out), .cin(pull_resistor_5_node));  // open: cout
  assign or_14_out = bit_extender_7_out | shifter_3_out;  // OR_Gate or_14, 10 bits wide
  Pull_Resistor pull_resistor_9 (.node(A_out_7));
  Pull_Resistor pull_resistor_10 (.node(B_out_7));
  Pull_Resistor pull_resistor_11 (.node(A_out_8));
  assign or_15_out = Program_Bank_Register_out_8 | Data_Bank_Register_out_8;  // OR_Gate or_15, 16 bits wide
  assign controlled_buffer_2_out = rom_1_data[13] ? Program_Counter_out_7 : 16'bz;  // Controlled_Buffer controlled_buffer_2
  _16BitRegister_main Program_Counter (
    .Data(multiplexer_3_out), .Store(rom_1_data[14]), .Clock(Clock), .Clear(Reset),
    .Enable_Output(pull_resistor_12_node), .Output_Select(pull_resistor_13_node),
    .out_7(Program_Counter_out_7));  // open: out_8
  Pull_Resistor #(.pull(1)) pull_resistor_12 (.node(pull_resistor_12_node));
  Pull_Resistor pull_resistor_13 (.node(pull_resistor_13_node));
  nor nor_1 (nor_1_out, rom_1_data_3[2], rom_1_data_3[1], rom_1_data_3[0]);
  not not_5 (not_5_out, or_16_out);
  or or_16 (or_16_out, rom_1_data[28], or_4_out[0], or_5_out[0], or_6_out[0], or_7_out[0], or_9_out[0]);
  not not_6 (not_6_out, or_8_out[0]);
  Pull_Resistor pull_resistor_14 (.node(C_out_7));
  Pull_Resistor pull_resistor_15 (.node(D_out_7));
  Pull_Resistor pull_resistor_16 (.node(Stack_Pointer_out_7));
  Pull_Resistor pull_resistor_17 (.node(Base_Pointer_out_7));
  Pull_Resistor pull_resistor_18 (.node(B_out_8));
  Pull_Resistor pull_resistor_19 (.node(C_out_8));
  Pull_Resistor pull_resistor_20 (.node(D_out_8));
  Pull_Resistor pull_resistor_21 (.node(Stack_Pointer_out_8));
  assign bit_extender_8_out = {{8{1'b0}}, or_15_out};  // Bit_Extender bit_extender_8
  Pull_Resistor pull_resistor_22 (.node(pull_resistor_22_node));
  Multiplexer #(.select(3), .enable("false")) multiplexer_4 (
    .in0(rom_1_data[12]), .in1(Flags_q[0]), .in2(not_8_out), .in3(Flags_q[1]), .in4(not_9_out),
    .in5(Flags_q[2]), .in6(not_7_out), .in7(not_10_out), .out(multiplexer_4_out), .sel(rom_1_data_3));
  not not_7 (not_7_out, Flags_q[2]);
  not not_8 (not_8_out, Flags_q[0]);
  not not_9 (not_9_out, Flags_q[1]);
  and and_3 (and_3_out, not_5_out, or_8_out[1], not_6_out);
  assign controlled_buffer_3_out = and_3_out ? 16'h2 : 16'bz;  // Controlled_Buffer controlled_buffer_3
  Pull_Resistor pull_resistor_23 (.node(Program_Bank_Register_out_7));
  Pull_Resistor pull_resistor_24 (.node(Data_Bank_Register_out_7));
  Pull_Resistor pull_resistor_25 (.node(controlled_buffer_3_out));
  Pull_Resistor pull_resistor_26 (.node(Base_Pointer_out_8));
  Pull_Resistor pull_resistor_27 (.node(controlled_buffer_2_out));
  Shifter #(.width(24)) shifter_4 (.in(bit_extender_8_out), .\dist (5'b10000), .out(shifter_4_out));
  Adder #(.width(16)) adder_2 (
    .a(Program_Counter_out_7), .b(controlled_buffer_4_out), .out(adder_2_out), .cin(pull_resistor_22_node));  // open: cout
  assign controlled_buffer_4_out = and_4_out ? 16'h2 : 16'bz;  // Controlled_Buffer controlled_buffer_4
  and and_4 (and_4_out, nor_1_out, multiplexer_4_out);
  not not_10 (not_10_out, Flags_q[3]);
  assign or_17_out = A_out_7 | B_out_7 | C_out_7 | D_out_7 | Stack_Pointer_out_7 | Base_Pointer_out_7 | Program_Bank_Register_out_7 | Data_Bank_Register_out_7;  // OR_Gate or_17, 16 bits wide
  assign or_18_out = A_out_8 | B_out_8 | C_out_8 | D_out_8 | controlled_buffer_3_out | Stack_Pointer_out_8 | Base_Pointer_out_8 | controlled_buffer_2_out | demultiplexer_3_out1;  // OR_Gate or_18, 16 bits wide
  assign or_19_out = shifter_4_out | bit_extender_9_out;  // OR_Gate or_19, 24 bits wide
  assign bit_extender_9_out = {{8{1'b0}}, Data_Out};  // Bit_Extender bit_extender_9
  Register #(.width(24)) Memory_Address_Register (
    .D(or_19_out), .en(rom_1_data[8]), .Q(Address_Bus), .clk(Clock), .clr(Reset));
  ALU_main ALU (
    .A_Input(or_17_out), .B_Input(or_18_out), .Op_Select(rom_1_data_2), .out_5(ALU_out_5), .Output(Data_Out));
  Register #(.width(4)) Flags (.D(ALU_out_5), .en(rom_1_data[7]), .Q(Flags_q), .clk(Clock), .clr(Reset));

  // Notes on the sheet:
  //   contents of rom_1 (hex, n*v repeats v):
  //   7802100 d002 0 8 14*0 c1800b4 8 14*0 c1800c4 8 14*0 c1800d4 8 14*0 c1800e4 8 14*0 c180084 8 14*0
  //   c180094 8 14*0 c1800a4 8 14*0 41800c4 8 14*0 8180004 8 14*0 7802100 17d00136 8005006 8 12*0 7802100
  //   17d00136 6005005 8 12*0 7802100 17c00102 8005006 8 12*0 7802100 17c00102 6005005 8 12*0 d1f0140
  //   6000005 8 13*0 71f0100 8000006 d000030 8 12*0 7802100 4002 8 13*0 7807100 4802 8 13*0 7807100 4602 8
  //   13*0 7807100 4402 8 13*0 7807100 4202 8 13*0 7807100 4c02 8 13*0 7807100 4a02 8 13*0 7802100
  //   140050c6 8 13*0 7807100 9c01002 7807100 4a02 5e60000 8 10*0 d1f0140 2001 7802100 4002 8 11*0 71f0100
  //   4002 d005030 8 12*0 7802100 1c0050b6 8 13*0 7802100 1c0050c6 8 13*0 7802100 1c0050d6 8 13*0 7802100
  //   1c0050e6 8 13*0 7802100 1c005086 8 13*0 7802100 1c005096 8 13*0 7802100 1c0050a6 8 13*0 7802100
  //   8005006 8
  //   29_Control_Lines
  //   Warning:_Terrible_wiring
endmodule
