// Logisim project FullSetup.circ as structural Verilog: 1 circuit, main circuit main
module main (
  input  in_1,
  input  [15:0] in_2,
  input  in_3,
  input  Reset,
  output [15:0] out_5,
  output [15:0] out_6,
  output [7:0] out_7
);

  wire and_1_out, and_2_out, and_3_out, bitselector_1_out, comparator_1_eq, comparator_2_eq, comparator_3_eq,
       keyboard_1_avail, main_1_read, main_1_write, Main_Clock_out, nor_1_out, or_1_out, or_2_out;
  wire [6:0] bit_extender_1_out, keyboard_1_data, pull_resistor_3_node;
  wire [7:0] multiplexer_1_out, multiplexer_2_out, ram_1_data, ram_2_data, ram_3_data, ram_4_data;
  wire [15:0] adder_1_out, bit_extender_3_out, bit_extender_4_out, multiplexer_3_out, multiplexer_4_out,
       multiplexer_5_out, multiplexer_7_out, pull_resistor_1_node;
  wire [23:0] main_1_address_bus, shifter_1_out;

  Adder #(.width(16)) adder_1 (.a(multiplexer_5_out), .b(16'h1), .out(adder_1_out));  // open: cin, cout
  BitSelector #(.width(16)) bitselector_1 (.in(multiplexer_5_out), .out(bitselector_1_out), .sel(4'b0000));
  Multiplexer #(.width(8), .enable("false")) multiplexer_1 (
    .in0(out_6[7:0]), .in1(out_6[15:8]), .out(multiplexer_1_out), .sel(bitselector_1_out));
  Multiplexer #(.width(8), .enable("false")) multiplexer_2 (
    .in0(out_6[15:8]), .in1(out_6[7:0]), .out(multiplexer_2_out), .sel(bitselector_1_out));
  Multiplexer #(.width(16), .enable("false")) multiplexer_3 (
    .in0(multiplexer_5_out), .in1(adder_1_out), .out(multiplexer_3_out), .sel(bitselector_1_out));
  Multiplexer #(.width(16), .enable("false")) multiplexer_4 (
    .in0(adder_1_out), .in1(multiplexer_5_out), .out(multiplexer_4_out), .sel(bitselector_1_out));
  RAM #(.addrWidth(16), .bus("separate")) ram_1 (
    .addr(multiplexer_3_out), .din(multiplexer_1_out), .data(ram_1_data), .str(main_1_write), .sel(or_1_out),
    .clk(Main_Clock_out), .ld(main_1_read), .clr(in_3));
  RAM #(.addrWidth(16), .bus("separate")) ram_2 (
    .addr(multiplexer_4_out), .din(multiplexer_2_out), .data(ram_2_data), .str(main_1_write), .sel(or_1_out),
    .clk(Main_Clock_out), .ld(main_1_read), .clr(in_3));
  RAM #(.addrWidth(16), .bus("separate")) ram_3 (
    .addr(multiplexer_3_out), .din(multiplexer_1_out), .data(ram_3_data), .str(main_1_write), .sel(or_2_out),
    .clk(Main_Clock_out), .ld(main_1_read));  // open: clr
  RAM #(.addrWidth(16), .bus("separate")) ram_4 (
    .addr(multiplexer_4_out), .din(multiplexer_2_out), .data(ram_4_data), .str(main_1_write), .sel(or_2_out),
    .clk(Main_Clock_out), .ld(main_1_read));  // open: clr
  Multiplexer #(.width(16), .enable("false")) multiplexer_5 (
    .in0(bit_extender_3_out), .in1(in_2), .out(multiplexer_5_out), .sel(in_1));
  Pull_Resistor pull_resistor_1 (.node(pull_resistor_1_node));
  Multiplexer #(.width(16), .enable("false")) multiplexer_6 (
    .in0({ram_2_data, ram_1_data}), .in1({ram_1_data, ram_2_data}), .out(pull_resistor_1_node),
    .sel(bitselector_1_out));
  or or_1 (or_1_out, in_1, comparator_2_eq);
  or or_2 (or_2_out, in_1, nor_1_out);
  Clock Main_Clock (.out(Main_Clock_out));
  Multiplexer #(.width(16), .enable("false")) multiplexer_7 (
    .in0({ram_4_data, ram_3_data}), .in1({ram_3_data, ram_4_data}), .out(multiplexer_7_out),
    .sel(bitselector_1_out));
  Pull_Resistor pull_resistor_2 (.node(multiplexer_7_out));
  assign out_5 = pull_resistor_1_node | bit_extender_4_out | multiplexer_7_out;  // OR_Gate or_3, 16 bits wide
  CPU_main main_1 (
    .Reset(Reset), .Clock(Main_Clock_out), .Data_In(out_5), .Data_Out(out_6),
    .Address_Bus(main_1_address_bus), .Read(main_1_read), .Write(main_1_write));
  nor nor_1 (nor_1_out, out_7[7], out_7[6], out_7[5], out_7[4], out_7[3], out_7[2], out_7[1], out_7[0]);
  Bit_Extender #(.in_width(16), .out_width(7)) bit_extender_1 (.in(out_6), .out(bit_extender_1_out));
  TTY tty_1 (.data(bit_extender_1_out), .clk(Main_Clock_out), .we(and_1_out), .clr(Reset));
  and and_1 (and_1_out, main_1_write, comparator_1_eq);
  Bit_Extender #(.in_width(24), .out_width(8)) bit_extender_2 (.in(shifter_1_out), .out(out_7));
  Shifter #(.width(24), .shift("lr")) shifter_1 (.in(main_1_address_bus), .\dist (5'b10000), .out(shifter_1_out));
  Bit_Extender #(.in_width(24)) bit_extender_3 (.in(main_1_address_bus), .out(bit_extender_3_out));
  Keyboard keyboard_1 (
    .clk(Main_Clock_out), .re(and_2_out), .clr(Reset), .avail(keyboard_1_avail), .data(keyboard_1_data));
  and and_2 (and_2_out, main_1_read, comparator_3_eq);
  Comparator comparator_1 (.a(out_7), .b(8'h2), .eq(comparator_1_eq));  // open: gt, lt
  Comparator comparator_2 (.a(out_7), .b(8'h1), .eq(comparator_2_eq));  // open: gt, lt
  Comparator comparator_3 (.a(out_7), .b(8'h3), .eq(comparator_3_eq));  // open: gt, lt
  assign bit_extender_4_out = {{9{1'b0}}, pull_resistor_3_node};  // Bit_Extender bit_extender_4
  Pull_Resistor pull_resistor_3 (.node(pull_resistor_3_node));
  assign pull_resistor_3_node = and_3_out ? keyboard_1_data : 7'bz;  // Controlled_Buffer controlled_buffer_1
  and and_3 (and_3_out, keyboard_1_avail, comparator_3_eq, main_1_read);
endmodule
